# Fritzing sketch Audio Effects Stereo (saved by Fritzing 0.9.3b)
breadboards: 1

parts:
  Adafruit_VS1053_Breakout_Board = Adafruit VS1053 Codec + MicroSD Breakout - MP3/WAV/MIDI/OGG [part_number="Adafruit #1381"]
  Arduino_Uno_R3 = Arduino Uno (Rev3) - ICSP
  Volume_and_Effects_Control = Rotary Potentiometer (Large) [maximum_resistance=100kΩ package=THT]
  WeMos_D1_Mini_OLED_Shield1 = WeMos D1 Mini OLED Shield
  Input = Audio Jack (TRS) 3.5mm [package="4Ucon 08780 [THT]"]
  Output = Audio Jack (TRS) 3.5mm [package="PG203J [THT]"]
  C1 = Electrolytic Capacitor [capacitance=1µF voltage=50V package="100 mil [THT, electrolytic]"]
  C2 = Electrolytic Capacitor [capacitance=1µF voltage=50V package="100 mil [THT, electrolytic]"]
  R2 = Resistor [tolerance=±5% resistance=10k package=THT]
  R3 = Resistor [tolerance=±5% resistance=10k package=THT]
  R4 = Resistor [tolerance=±5% resistance=470 package=THT]
  R5 = Resistor [tolerance=±5% resistance=10k package=THT]
  R6 = Resistor [tolerance=±5% resistance=10k package=THT]
  Function_Select = Pushbutton [package="[THT]"]
  Increase = Pushbutton [package="[THT]"]
  Decrease = Pushbutton [package="[THT]"]
  R7 = Resistor [tolerance=±5% resistance=10k package=THT]
  Effects_On/Off_Foot_Switch = Round Pushbutton
  R8 = Resistor [tolerance=±5% resistance=10k package=THT]
  Effects_Off_LED = LED - 5mm [color="Yellow (595nm)" package="5 mm [THT]"]
  R9 = Resistor [tolerance=±5% resistance=470 package=THT]
  Loop_Activity_LED = LED - 5mm [color="Red (633nm)" package="5 mm [THT]"]
  R10 = Resistor [tolerance=±5% resistance=470 package=THT]

nets:
  N1: Adafruit_VS1053_Breakout_Board.R_OUT, Output.Tip
  N2: Adafruit_VS1053_Breakout_Board.L_OUT, Output.Ring
  N3: Adafruit_VS1053_Breakout_Board.AGND, Output.Sleeve
  GND: Adafruit_VS1053_Breakout_Board.GND, Arduino_Uno_R3.GND, Volume_and_Effects_Control.leg1, WeMos_D1_Mini_OLED_Shield1.G, Input.Sleeve, R2.Pin_0, R3.Pin_0, R5.Pin_0, R6.Pin_0, R7.Pin_0, R8.Pin_1, R9.Pin_1, R10.Pin_1
  N4: Adafruit_VS1053_Breakout_Board.DREQ, Arduino_Uno_R3.D2
  VIN: Adafruit_VS1053_Breakout_Board.VIN, Arduino_Uno_R3.5V, Volume_and_Effects_Control.leg2, Function_Select.Pin_1, Function_Select.Pin_2, Increase.Pin_1, Increase.Pin_2, Decrease.Pin_1, Decrease.Pin_2
  N5: Adafruit_VS1053_Breakout_Board.3.3V, Effects_On/Off_Foot_Switch.leg0
  N6: Adafruit_VS1053_Breakout_Board.MISO, Arduino_Uno_R3.D12/MISO
  N7: Adafruit_VS1053_Breakout_Board.MOSI_5V, Arduino_Uno_R3.D11_PWM/MOSI
  N8: Adafruit_VS1053_Breakout_Board.SCLK_5V, Arduino_Uno_R3.D13/SCK
  N9: Adafruit_VS1053_Breakout_Board.RST_5V, Arduino_Uno_R3.D8
  N10: Adafruit_VS1053_Breakout_Board.CS_5V, Arduino_Uno_R3.D6_PWM
  N11: Adafruit_VS1053_Breakout_Board.XDCS_5V, Arduino_Uno_R3.D7
  N12: Adafruit_VS1053_Breakout_Board.LINE2, C1.-, R3.Pin_1
  N13: Adafruit_VS1053_Breakout_Board.MIC_P, C2.-, R2.Pin_1
  N14: Adafruit_VS1053_Breakout_Board.GPIO3, Effects_On/Off_Foot_Switch.leg1, R8.Pin_0
  N15: Arduino_Uno_R3.A0, R4.Pin_0
  N16: Arduino_Uno_R3.D9_PWM, R5.Pin_1, Function_Select.Pin_3, Function_Select.Pin_4
  N17: Arduino_Uno_R3.D10_PWM/SS, Loop_Activity_LED.cathode, R10.Pin_0
  N18: Arduino_Uno_R3.A4/SDA, WeMos_D1_Mini_OLED_Shield1.D2
  N19: Arduino_Uno_R3.A5/SCL, WeMos_D1_Mini_OLED_Shield1.D1
  N20: Arduino_Uno_R3.D3_PWM, Decrease.Pin_3, Decrease.Pin_4, R7.Pin_1
  N21: Arduino_Uno_R3.D4, Effects_Off_LED.anode
  N22: Arduino_Uno_R3.D5_PWM, R6.Pin_1, Increase.Pin_3, Increase.Pin_4
  3V3: Arduino_Uno_R3.3V3, WeMos_D1_Mini_OLED_Shield1.3V3
  N23: Volume_and_Effects_Control.wiper, R4.Pin_1
  N24: Input.Ring, C1.+
  N25: Input.Tip, C2.+
  N26: Effects_Off_LED.cathode, R9.Pin_0

custom parts:
  Adafruit VS1053 Codec + MicroSD Breakout - MP3/WAV/MIDI/OGG: This breakout board is the ultimate companion for the VLSI VS1053B DSP codec chip. The VS1053 can decode a wide variety of audio formats such as MP3, AAC, Ogg Vorbis, WMA, MIDI, FLAC, WAV (PCM and ADPCM). It can also be used to record audio in both PCM (WAV) and compressed Ogg Vorbis. You can do all sorts of stuff with the audio as well such as adjusting bass, treble, and volume digitally.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
